// Logisim project Somadores.circ as structural Verilog: 5 circuits, main circuit main
module main (
  input  [3:0] in_1,
  input  [3:0] in_2,
  output out_3,
  output [3:0] out_4
);

  Somador_4Bits somador_4bits_1 (.Overflow(out_3), .B(in_2), .A(in_1), .Saida(out_4));
endmodule

module Somador_1Bit (
  input  A,
  input  B,
  input  C,
  output S,
  output Vai_1
);

  wire and_1_out, and_2_out, or_1_out, xor_1_out;

  xor xor_1 (xor_1_out, C, B);
  and and_1 (and_1_out, C, B);
  or or_1 (or_1_out, C, B);
  and and_2 (and_2_out, or_1_out, A);
  xor xor_2 (S, xor_1_out, A);
  or or_2 (Vai_1, and_1_out, and_2_out);
endmodule

module Somador_4Bits (
  input  [3:0] A,
  input  [3:0] B,
  output Overflow,
  output [3:0] Saida
);

  wire somador_1bit_2_vai_1, somador_1bit_3_vai_1, somador_1bit_4_vai_1;

  // Probe on B
  Somador_1Bit somador_1bit_1 (.S(Saida[3]), .Vai_1(Overflow), .A(A[3]), .B(B[3]), .C(somador_1bit_2_vai_1));
  Somador_1Bit somador_1bit_2 (
    .S(Saida[2]), .Vai_1(somador_1bit_2_vai_1), .A(A[2]), .B(B[2]), .C(somador_1bit_3_vai_1));
  // Probe on Saida
  Somador_1Bit somador_1bit_3 (
    .S(Saida[1]), .Vai_1(somador_1bit_3_vai_1), .A(A[1]), .B(B[1]), .C(somador_1bit_4_vai_1));
  Somador_1Bit somador_1bit_4 (.S(Saida[0]), .Vai_1(somador_1bit_4_vai_1), .A(A[0]), .B(B[0]), .C(1'b0));
  // Probe on A
endmodule

module Subtrator_1Bit (
  input  A,
  input  B,
  input  C,
  output S,
  output Vai_1
);

  wire and_1_out, and_2_out, or_1_out, xor_1_out;

  xor xor_1 (xor_1_out, C, B);
  and and_1 (and_1_out, C, B);
  or or_1 (or_1_out, C, B);
  and and_2 (and_2_out, or_1_out, ~A);  // AND_Gate
  xor xor_2 (S, xor_1_out, A);
  or or_2 (Vai_1, and_1_out, and_2_out);
endmodule

module Subtrator_4Bit (
  input  [3:0] A,
  input  [3:0] B,
  output Overflow,
  output [3:0] Saida
);

  wire subtrator_1bit_2_vai_1, subtrator_1bit_3_vai_1, subtrator_1bit_4_vai_1;

  // Probe on B
  Subtrator_1Bit subtrator_1bit_1 (.S(Saida[3]), .Vai_1(Overflow), .A(A[3]), .B(B[3]), .C(subtrator_1bit_2_vai_1));
  Subtrator_1Bit subtrator_1bit_2 (
    .S(Saida[2]), .Vai_1(subtrator_1bit_2_vai_1), .A(A[2]), .B(B[2]), .C(subtrator_1bit_3_vai_1));
  // Probe on Saida
  Subtrator_1Bit subtrator_1bit_3 (
    .S(Saida[1]), .Vai_1(subtrator_1bit_3_vai_1), .A(A[1]), .B(B[1]), .C(subtrator_1bit_4_vai_1));
  Subtrator_1Bit subtrator_1bit_4 (.S(Saida[0]), .Vai_1(subtrator_1bit_4_vai_1), .A(A[0]), .B(B[0]), .C(1'b0));
  // Probe on A
endmodule
